# Fritzing sketch esp8266_01s (saved by Fritzing 0.9.3b)

parts:
  v = AC Power [voltage=220 frequency=60]
  V1 = DC Power [voltage=3.3V]
  Hue_Light = LEDs [package=led10mm]
  Wall_switch = SWITCH-MOMENTARY-2 [package=reed_switch_plastic]
  220v_to_3_3v = Transformer [package=transformer_smd]
  part = ESP8266 WiFi Module [part_number="ESP8266 01s"]
  R1 = Resistor [tolerance=±5% resistance=10k package="2010 [SMD]"]

nets (from the schematic view):
  N1: v.V+, 220v_to_3_3v.1
  N2: v.V-, Hue_Light.A
  N3: V1.V+, 220v_to_3_3v.4, part.VCC, R1.Pin_0
  N4: V1.V-, Wall_switch.1, 220v_to_3_3v.3, part.GND
  GND: Hue_Light.C, 220v_to_3_3v.2
  N5: Wall_switch.2, part.GPIO_0, R1.Pin_1

custom parts:
  ESP8266 WiFi Module: Generic WiFi Module based on the ESP8266 with onboard PCB antenna and UART communications
